# Fritzing sketch joystick-servo (saved by Fritzing 0.9.3b)
breadboards: 1

parts:
  Componente1 = Thumb Joystick
  J1 = Basic Servo
  Componente2 = Arduino Uno (Rev3)

nets:
  GND: Componente1.GND, Componente2.GND
  N1: Componente1.VERT, Componente2.A0
  VCC: Componente1.VCC, J1.vcc, Componente2.5V
  N2: J1.pulse, Componente2.D10_PWM/SS
