# Fritzing sketch fritzing_v2 (saved by Fritzing 0.9.3b)
breadboards: 1

parts:
  LED1 = LED - 3mm [color="Yellow (595nm)" package="3 mm [THT]"]
  LED2 = LED - 3mm [color="Green (570nm)" package="3 mm [THT]"]
  LED3 = LED - 3mm [color="Red (633nm)" package="3 mm [THT]"]
  LED4 = LED - 3mm [color="Yellow (595nm)" package="3 mm [THT]"]
  LED5 = LED - 3mm [color="Green (570nm)" package="3 mm [THT]"]
  LED6 = LED - 3mm [color="Red (633nm)" package="3 mm [THT]"]
  LED7 = LED - 3mm [color="Yellow (595nm)" package="3 mm [THT]"]
  LED8 = LED - 3mm [color="Green (570nm)" package="3 mm [THT]"]
  LED9 = LED - 3mm [color="Red (633nm)" package="3 mm [THT]"]
  R1 = Resistor [tolerance=±5% resistance=220 package=THT]
  Componente1 = Arduino Uno (Rev3)

nets:
  N1: LED1.cathode, LED2.cathode, LED3.cathode, LED4.cathode, LED5.cathode, LED6.cathode, LED7.cathode, LED8.cathode, LED9.cathode, R1.Pin_0
  N2: LED1.anode, Componente1.D12/MISO
  N3: LED2.anode, Componente1.D11_PWM/MOSI
  N4: LED3.anode, Componente1.D10_PWM/SS
  N5: LED4.anode, Componente1.D9_PWM
  N6: LED5.anode, Componente1.D8
  N7: LED6.anode, Componente1.D7
  N8: LED7.anode, Componente1.D6_PWM
  N9: LED8.anode, Componente1.D5_PWM
  N10: LED9.anode, Componente1.D4
  N11: R1.Pin_1, Componente1.GND
