# Fritzing sketch fritzing2 (saved by Fritzing 0.9.3b)
breadboards: 1

parts:
  R1 = Resistor [tolerance=±5% resistance=220 package=THT]
  LED1 = LED - 5mm [color="Red (633nm)" package="5 mm [THT]"]
  R2 = Resistor [tolerance=±5% resistance=220 package=THT]
  S1 = Pushbutton [package="[THT]"]
  Componente1 = Arduino Uno (Rev3)

nets:
  N1: R1.Pin_0, LED1.cathode
  N2: R1.Pin_1, R2.Pin_1, Componente1.GND
  N3: LED1.anode, Componente1.D13/SCK
  N4: R2.Pin_0, S1.Pin_3, S1.Pin_4, Componente1.D2
  N5: S1.Pin_1, S1.Pin_2, Componente1.5V
