# Fritzing sketch fritzing2 (saved by Fritzing 0.9.3b)
breadboards: 1

parts:
  LED1 = LED - 3mm [color="Red (633nm)" package="3 mm [THT]"]
  LED2 = LED - 3mm [color="Yellow (595nm)" package="3 mm [THT]"]
  LED3 = LED - 3mm [color="Green (570nm)" package="3 mm [THT]"]
  LED4 = LED - 3mm [color="Red (633nm)" package="3 mm [THT]"]
  LED5 = LED - 3mm [color="Green (570nm)" package="3 mm [THT]"]
  S1 = Pushbutton [package="[THT]"]
  R1 = Resistor [tolerance=±5% resistance=220 package=THT]
  R2 = Resistor [tolerance=±5% resistance=220 package=THT]
  R3 = Resistor [tolerance=±5% resistance=220 package=THT]
  R4 = Resistor [tolerance=±5% resistance=220 package=THT]
  R5 = Resistor [tolerance=±5% resistance=220 package=THT]
  R6 = Resistor [tolerance=±5% resistance=10k package=THT]
  Componente1 = Arduino Uno (Rev3)

nets:
  N1: LED1.cathode, R1.Pin_0
  N2: LED1.anode, Componente1.D13/SCK
  N3: LED2.cathode, R2.Pin_0
  N4: LED2.anode, Componente1.D12/MISO
  N5: LED3.cathode, R3.Pin_0
  N6: LED3.anode, Componente1.D11_PWM/MOSI
  N7: LED4.cathode, R4.Pin_0
  N8: LED4.anode, Componente1.D10_PWM/SS
  N9: LED5.cathode, R5.Pin_0
  N10: LED5.anode, Componente1.D9_PWM
  N11: S1.Pin_2, Componente1.5V
  N12: S1.Pin_4, R6.Pin_0, Componente1.D2
  N13: R1.Pin_1, R2.Pin_1, R3.Pin_1, R4.Pin_1, R5.Pin_1, R6.Pin_1, Componente1.GND
