# Fritzing sketch semaforo_simple (saved by Fritzing 0.9.3b)
breadboards: 1

parts:
  R1 = Resistor [tolerance=±5% resistance=220 package=THT]
  R2 = Resistor [tolerance=±5% resistance=220 package=THT]
  R3 = Resistor [tolerance=±5% resistance=220 package=THT]
  Componente1 = Arduino Uno (Rev3)
  LED3 = LED - 5mm [color="Green (565nm)" package="5 mm [THT]"]
  LED2 = smd LED [color="Red (633nm)" package="0603 [SMD]"]
  LED4 = LED - 5mm [color="Yellow (585nm)" package="5 mm [THT]"]

nets:
  N1: R1.Pin_0, Componente1.D4
  N2: R1.Pin_1, LED2.anode
  N3: R2.Pin_0, Componente1.D5_PWM
  N4: R2.Pin_1, LED4.anode
  N5: R3.Pin_0, Componente1.D6_PWM
  N6: R3.Pin_1, LED3.anode
  N7: Componente1.GND, LED3.cathode, LED2.cathode, LED4.cathode
